// Logisim project 8-Bit-Adder.circ as structural Verilog: 3 circuits, main circuit main
module main (
  input  A,
  input  B,
  input  Cout,
  input  A_2,
  input  B_2,
  input  A_3,
  input  B_3,
  input  A_4,
  input  B_4,
  input  A_5,
  input  B_5,
  input  A_6,
  input  B_6,
  input  A_7,
  input  B_7,
  input  A_8,
  input  B_8,
  output Sum,
  output Sum_2,
  output Sum_3,
  output Sum_4,
  output Sum_5,
  output Sum_6,
  output Sum_7,
  output Sum_8,
  output Cout_Final
);

  wire one_bit_adder_1_cout, one_bit_adder_2_cout, one_bit_adder_3_cout, one_bit_adder_4_cout,
       one_bit_adder_5_cout, one_bit_adder_6_cout, one_bit_adder_7_cout;

  One_Bit_Adder one_bit_adder_1 (.A(A), .B(B), .Cin(Cout), .Sum(Sum), .Cout(one_bit_adder_1_cout));
  One_Bit_Adder one_bit_adder_2 (
    .A(A_2), .B(B_2), .Cin(one_bit_adder_1_cout), .Sum(Sum_2), .Cout(one_bit_adder_2_cout));
  One_Bit_Adder one_bit_adder_3 (
    .A(A_3), .B(B_3), .Cin(one_bit_adder_2_cout), .Sum(Sum_3), .Cout(one_bit_adder_3_cout));
  One_Bit_Adder one_bit_adder_4 (
    .A(A_4), .B(B_4), .Cin(one_bit_adder_3_cout), .Sum(Sum_4), .Cout(one_bit_adder_4_cout));
  One_Bit_Adder one_bit_adder_5 (
    .A(A_5), .B(B_5), .Cin(one_bit_adder_4_cout), .Sum(Sum_5), .Cout(one_bit_adder_5_cout));
  One_Bit_Adder one_bit_adder_6 (
    .A(A_6), .B(B_6), .Cin(one_bit_adder_5_cout), .Sum(Sum_6), .Cout(one_bit_adder_6_cout));
  One_Bit_Adder one_bit_adder_7 (
    .A(A_7), .B(B_7), .Cin(one_bit_adder_6_cout), .Sum(Sum_7), .Cout(one_bit_adder_7_cout));
  One_Bit_Adder one_bit_adder_8 (.A(A_8), .B(B_8), .Cin(one_bit_adder_7_cout), .Sum(Sum_8), .Cout(Cout_Final));
endmodule

module _1_Bit_Adder (
  input  Cin,
  input  B,
  input  A,
  output Sum,
  output Cout
);

  wire and_1_out, and_2_out, and_3_out, and_4_out, and_5_out, and_6_out, and_7_out, not_1_out, not_2_out,
       not_3_out, not_4_out, not_5_out, not_6_out;

  not not_1 (not_1_out, A);
  not not_2 (not_2_out, B);
  not not_3 (not_3_out, A);
  not not_4 (not_4_out, B);
  and and_1 (and_1_out, not_2_out, B, not_3_out);
  and and_2 (and_2_out, not_3_out, B, not_5_out);
  not not_5 (not_5_out, B);
  and and_3 (and_3_out, A, not_2_out, not_5_out);
  and and_4 (and_4_out, A, B, B);
  and and_5 (and_5_out, not_1_out, B, B);
  and and_6 (and_6_out, A, not_4_out, B);
  and and_7 (and_7_out, B, not_6_out);
  not not_6 (not_6_out, B);
  or or_1 (Sum, and_1_out, and_2_out, and_3_out, and_4_out);
  or or_2 (Cout, and_5_out, and_6_out, and_7_out);

  assign Cin = B;
endmodule

module One_Bit_Adder (
  input  A,
  input  B,
  input  Cin,
  output Sum,
  output Cout
);

  wire and_1_out, and_2_out, and_3_out, and_4_out, and_5_out, and_6_out, and_7_out, and_8_out, not_1_out,
       not_2_out, not_3_out, not_4_out, not_5_out, not_6_out;

  not not_1 (not_1_out, Cin);
  not not_2 (not_2_out, A);
  not not_3 (not_3_out, B);
  not not_4 (not_4_out, A);
  not not_5 (not_5_out, B);
  not not_6 (not_6_out, Cin);
  and and_1 (and_1_out, not_2_out, not_3_out, Cin);
  and and_2 (and_2_out, not_2_out, B, not_1_out);
  and and_3 (and_3_out, A, not_3_out, not_1_out);
  and and_4 (and_4_out, A, B, Cin);
  and and_5 (and_5_out, not_4_out, B, Cin);
  and and_6 (and_6_out, A, not_5_out, Cin);
  and and_7 (and_7_out, A, B, not_6_out);
  and and_8 (and_8_out, A, B, Cin);
  or or_1 (Sum, and_1_out, and_2_out, and_3_out, and_4_out);
  or or_2 (Cout, and_5_out, and_6_out, and_7_out, and_8_out);
endmodule
