// Logisim project 8-Bit-Register.circ as structural Verilog: 3 circuits, main circuit Dlatch
module Dlatch (
  input  D,
  input  C,
  input  E,
  output Q
);

  wire and_1_out, and_2_out, and_3_out, not_1_out, not_2_out, or_1_out, or_2_out;

  not not_1 (not_1_out, D);
  buf and_1 (and_1_out, E);  // AND_Gate
  buf and_2 (and_2_out, and_1_out);  // AND_Gate
  buf and_3 (and_3_out, and_1_out);  // AND_Gate
  or or_1 (or_1_out, and_2_out, Q);
  or or_2 (or_2_out, not_2_out, and_3_out);
  not not_2 (not_2_out, or_1_out);
  not not_3 (Q, or_2_out);
endmodule

module _8_Bit_Register (
  input  in_1,
  input  in_2,
  input  in_3,
  input  in_4,
  input  in_5,
  input  in_6,
  input  in_7,
  input  in_8,
  input  E,
  output out_10,
  output out_11,
  output out_12,
  output out_13,
  output out_14,
  output out_15,
  output out_16,
  output out_17
);

  wire Cl_out;

  Button Cl (.out(Cl_out));
  Dlatch dlatch_1 (.D(in_1), .C(E), .E(Cl_out), .Q(out_10));
  Dlatch dlatch_2 (.D(in_2), .C(E), .E(Cl_out), .Q(out_11));
  Dlatch dlatch_3 (.D(in_3), .C(E), .E(Cl_out), .Q(out_12));
  Dlatch dlatch_4 (.D(in_4), .C(E), .E(Cl_out), .Q(out_13));
  Dlatch dlatch_5 (.D(in_5), .C(E), .E(Cl_out), .Q(out_14));
  Dlatch dlatch_6 (.D(in_6), .C(E), .E(Cl_out), .Q(out_15));
  Dlatch dlatch_7 (.D(in_7), .C(E), .E(Cl_out), .Q(out_16));
  Dlatch dlatch_8 (.D(in_8), .C(E), .E(Cl_out), .Q(out_17));
endmodule

module _1_bit_register (
  input  in_1,
  input  in_2,
  input  in_3,
  input  in_4,
  output out_5
);

  wire or_1_out, or_2_out;

  and and_1 (out_5, in_2, in_3);
  buf or_1 (or_1_out, in_1);  // OR_Gate
  buf or_2 (or_2_out, in_4);  // OR_Gate
  // NOT_Gate not_1 has open pins: in=or_1_out, out=open
  // NOT_Gate not_2 has open pins: in=or_2_out, out=open
endmodule
