// Logisim project 8bitregister.circ as structural Verilog: 2 circuits, main circuit main
module main (
  input  D,
  input  C,
  input  E,
  output out_4
);

  wire and_1_out, and_2_out, and_3_out, not_1_out, not_3_out, or_1_out, or_2_out;

  and and_1 (and_1_out, C, E);
  not not_1 (not_1_out, D);
  and and_2 (and_2_out, D, and_1_out);
  and and_3 (and_3_out, and_1_out, not_1_out);
  or or_1 (or_1_out, and_2_out, not_3_out);
  or or_2 (or_2_out, out_4, and_3_out);
  not not_2 (out_4, or_1_out);
  not not_3 (not_3_out, or_2_out);
endmodule

module _8_Bit_Register (
  input  in_1,
  input  in_2,
  input  in_3,
  input  in_4,
  input  in_5,
  input  in_6,
  input  in_7,
  input  in_8,
  input  in_9,
  output out_10,
  output out_11,
  output out_12,
  output out_13,
  output out_14,
  output out_15,
  output out_16,
  output out_17
);

  wire button_1_out;

  Button button_1 (.out(button_1_out));
  main main_1 (.D(in_1), .C(button_1_out), .E(in_9), .out_4(out_10));
  main main_2 (.D(in_2), .C(in_9), .E(button_1_out), .out_4(out_11));
  main main_3 (.D(in_3), .C(in_9), .E(button_1_out), .out_4(out_12));
  main main_4 (.D(in_4), .C(in_9), .E(button_1_out), .out_4(out_13));
  main main_5 (.D(in_5), .C(in_9), .E(button_1_out), .out_4(out_14));
  main main_6 (.D(in_6), .C(in_9), .E(button_1_out), .out_4(out_15));
  main main_7 (.D(in_7), .C(in_9), .E(button_1_out), .out_4(out_16));
  main main_8 (.D(in_8), .C(in_9), .E(button_1_out), .out_4(out_17));
endmodule
