// Logisim project demmo 1.circ as structural Verilog: 7 circuits, main circuit main
module main (
  input  A,
  input  B,
  output out_3
);

  wire and_1_out, and_2_out, not_1_out, not_2_out;

  not not_1 (not_1_out, A);
  not not_2 (not_2_out, B);
  buf and_1 (and_1_out, B);  // AND_Gate
  and and_2 (and_2_out, A, not_2_out);
  or or_1 (out_3, and_1_out, and_2_out);
  LED led_1 (.in(out_3));
endmodule

module coolcircut (
);

  main main_1 ();  // open: A, B, out_3
  main main_2 ();  // open: A, B, out_3
endmodule

module onebitfulladder (
  input  A,
  input  B,
  input  Cin,
  output Sum,
  output Cout
);

  wire and_1_out, and_2_out, and_3_out, and_4_out, and_5_out, and_6_out, and_7_out, and_8_out, not_1_out,
       not_2_out, not_3_out, not_4_out, not_5_out, not_6_out;

  not not_1 (not_1_out, B);
  not not_2 (not_2_out, Cin);
  not not_3 (not_3_out, A);
  not not_4 (not_4_out, B);
  not not_5 (not_5_out, Cin);
  not not_6 (not_6_out, A);
  and and_1 (and_1_out, not_6_out, not_1_out, Cin);
  and and_2 (and_2_out, not_6_out, B, not_2_out);
  and and_3 (and_3_out, A, B, Cin);
  and and_4 (and_4_out, not_3_out, B, Cin);
  and and_5 (and_5_out, A, not_4_out, Cin);
  and and_6 (and_6_out, A, B, not_5_out);
  and and_7 (and_7_out, A, B, Cin);
  and and_8 (and_8_out, A, not_1_out, not_2_out);
  or or_1 (Sum, and_1_out, and_2_out, and_8_out, and_3_out);
  or or_2 (Cout, and_4_out, and_5_out, and_6_out, and_7_out);
endmodule

module _8bitadder (
  input  A,
  input  B,
  input  Cout,
  input  A_2,
  input  B_2,
  input  A_3,
  input  B_3,
  input  A_4,
  input  B_4,
  input  A_5,
  input  B_5,
  input  A_6,
  input  B_6,
  input  A_7,
  input  B_7,
  input  A_8,
  input  B_8,
  output Sum,
  output Sum_2,
  output Sum_3,
  output Sum_4,
  output Sum_5,
  output Sum_6,
  output Sum_7,
  output Sum_8,
  output Cout_Final
);

  wire onebitfulladder_1_cout, onebitfulladder_2_cout, onebitfulladder_3_cout, onebitfulladder_4_cout,
       onebitfulladder_5_cout, onebitfulladder_6_cout, onebitfulladder_7_cout;

  onebitfulladder onebitfulladder_1 (.A(A), .B(B), .Cin(Cout), .Sum(Sum), .Cout(onebitfulladder_1_cout));
  onebitfulladder onebitfulladder_2 (
    .A(A_2), .B(B_2), .Cin(onebitfulladder_1_cout), .Sum(Sum_2), .Cout(onebitfulladder_2_cout));
  onebitfulladder onebitfulladder_3 (
    .A(A_3), .B(B_3), .Cin(onebitfulladder_2_cout), .Sum(Sum_3), .Cout(onebitfulladder_3_cout));
  onebitfulladder onebitfulladder_4 (
    .A(A_4), .B(B_4), .Cin(onebitfulladder_3_cout), .Sum(Sum_4), .Cout(onebitfulladder_4_cout));
  onebitfulladder onebitfulladder_5 (
    .A(A_5), .B(B_5), .Cin(onebitfulladder_4_cout), .Sum(Sum_5), .Cout(onebitfulladder_5_cout));
  onebitfulladder onebitfulladder_6 (
    .A(A_6), .B(B_6), .Cin(onebitfulladder_5_cout), .Sum(Sum_6), .Cout(onebitfulladder_6_cout));
  onebitfulladder onebitfulladder_7 (
    .A(A_7), .B(B_7), .Cin(onebitfulladder_6_cout), .Sum(Sum_7), .Cout(onebitfulladder_7_cout));
  onebitfulladder onebitfulladder_8 (.A(A_8), .B(B_8), .Cin(onebitfulladder_7_cout), .Sum(Sum_8), .Cout(Cout_Final));
endmodule

module ORfeedback (
  input  A,
  input  B,
  output D,
  output E
);

  wire or_1_out, or_2_out;

  or or_1 (or_1_out, A, E);
  or or_2 (or_2_out, B, D);
  not not_1 (D, or_1_out);
  not not_2 (E, or_2_out);
endmodule

module dlatch (
  input  D,
  input  C,
  input  E,
  output Q
);

  wire and_1_out, and_2_out, and_3_out, not_1_out, not_3_out, or_1_out, or_2_out;

  and and_1 (and_1_out, C, E);
  not not_1 (not_1_out, D);
  and and_2 (and_2_out, D, and_1_out);
  and and_3 (and_3_out, and_1_out, not_1_out);
  or or_1 (or_1_out, and_2_out, not_3_out);
  or or_2 (or_2_out, and_3_out, Q);
  not not_2 (Q, or_1_out);
  not not_3 (not_3_out, or_2_out);
endmodule

module _8bitregister (
  input  in_1,
  input  in_2,
  input  in_3,
  input  in_4,
  input  in_5,
  input  in_6,
  input  in_7,
  input  in_8,
  input  E,
  output out_10,
  output out_11,
  output out_12,
  output out_13,
  output out_14,
  output out_15,
  output out_16,
  output out_17
);

  wire CL_out;

  Button CL (.out(CL_out));
  dlatch dlatch_1 (.D(in_1), .C(CL_out), .E(E), .Q(out_10));
  dlatch dlatch_2 (.D(in_2), .C(E), .E(CL_out), .Q(out_11));
  dlatch dlatch_3 (.D(E), .C(E), .E(CL_out), .Q(out_12));
  dlatch dlatch_4 (.D(in_4), .C(E), .E(CL_out), .Q(out_13));
  dlatch dlatch_5 (.D(in_5), .C(E), .E(CL_out), .Q(out_14));
  dlatch dlatch_6 (.D(in_6), .C(E), .E(CL_out), .Q(out_15));
  dlatch dlatch_7 (.D(in_7), .C(E), .E(CL_out), .Q(out_16));
  dlatch dlatch_8 (.D(in_8), .C(E), .E(CL_out), .Q(out_17));

  assign in_3 = E;
endmodule
